# Fritzing sketch blender (saved by Fritzing 0.9.2b)
circuit board: 8.46667cm x 5.64444cm
breadboards: 1

parts:
  Raspberry_Pi1 = Raspberry Pi B rev2
  IC2 = IC, DIP package, 40 pins [chip_label=WDC65C02S spacing=600mil]

nets:
  N1: Raspberry_Pi1.3V3, IC2.pin8
  N2: Raspberry_Pi1.GPIO_2, IC2.pin9
  N3: Raspberry_Pi1.GPIO_3, IC2.pin10
  N4: Raspberry_Pi1.GND, IC2.pin21
  N5: Raspberry_Pi1.GPIO_23, IC2.pin23
  N6: Raspberry_Pi1.GPIO_14, IC2.pin17
  N7: Raspberry_Pi1.GPIO_15, IC2.pin18
  N8: Raspberry_Pi1.GPIO_17, IC2.pin19
  N9: Raspberry_Pi1.GPIO_18, IC2.pin20
  N10: Raspberry_Pi1.GPIO_22, IC2.pin22
  N11: Raspberry_Pi1.GPIO_4, IC2.pin11
  N12: Raspberry_Pi1.GPIO_24, IC2.pin24
  N13: Raspberry_Pi1.GPIO_10, IC2.pin15
  N14: Raspberry_Pi1.GPIO_9, IC2.pin14
  N15: Raspberry_Pi1.GPIO_25, IC2.pin25
  N16: Raspberry_Pi1.GPIO_11, IC2.pin16
  N17: Raspberry_Pi1.GPIO_8, IC2.pin13
  N18: Raspberry_Pi1.GPIO_7, IC2.pin12
